# Fritzing sketch teensy_atmega (saved by Fritzing 0.9.4)
breadboards: 2

parts:
  Teensy1 = Teensy 2.0
  Part1 = SPI OLED Monochrome 128x64 0.96 inch
  LED3 = smd LED [color="Yellow (595nm)" package="1206 [SMD]"]  # not connected
  LED4 = smd LED [color="Green (555nm)" package="0805 [SMD]"]  # not connected

nets:
  GND: Teensy1.GND, Part1.GND
  N1: Teensy1.B1, Part1.SCK
  N2: Teensy1.B7, Part1.RES
  N3: Teensy1.D1, Part1.SDA
  VCC: Teensy1.VCC, Part1.VDD

custom parts:
  SPI OLED Monochrome 128x64 0.96 inch: Unknown 128x64 0.96 inch 128x64 SPI Monochrome OLED display
