# Fritzing sketch initial Circuit Design (saved by Fritzing 0.9.4)
breadboards: 1

parts:
  Teensy1 = Teensy 2.0
  Part1 = SPI OLED Monochrome 128x64 0.96 inch
  S1 = Tactile Switch Buttons - 12mm Square [package=tactile-pth-12mm]
  S2 = Tactile Switch Buttons - 12mm Square [package=tactile-pth-12mm]  # not connected
  S3 = Tactile Switch Buttons - 12mm Square [package=tactile-pth-12mm]
  S4 = Tactile Switch Buttons - 12mm Square [package=tactile-pth-12mm]
  S5 = Tactile Switch Buttons - 12mm Square [package=tactile-pth-12mm]
  S6 = Tactile Switch Buttons - 12mm Square [package=tactile-pth-12mm]

nets:
  GND: Teensy1.GND, Part1.GND, S1.2, S1.4
  N1: Teensy1.B1, Part1.SCK
  N2: Teensy1.D1, Part1.SDA
  N3: Teensy1.D4, Part1.DC
  N4: Teensy1.D6, Part1.CS
  N5: Teensy1.D7, Part1.RES
  N6: Teensy1.B4, S1.1, S1.3
  N7: Teensy1.F7, S4.1
  N8: Teensy1.F6, S5.1, S5.3
  N9: Teensy1.F5, S3.1, S3.3
  N10: Teensy1.F4, S6.1, S6.3
  VCC: Teensy1.VCC, Part1.VDD
  N11: S3.2, S3.4, S4.2, S4.4, S5.2, S5.4, S6.2

custom parts:
  SPI OLED Monochrome 128x64 0.96 inch: Unknown 128x64 0.96 inch 128x64 SPI Monochrome OLED display
  Tactile Switch Buttons - 12mm Square: Medium-sized clicky momentary switches are standard input "buttons" on electronic projects. These work best in a PCB but can be used on a solderless breadboard as shown in this tutorial. The pins are normally open (disconnected) and when the button is pressed they are momentarily closed. They come in a pack of 10, they're pretty handy so you'll want to keep them around. You can find an EAGLE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
